# Fritzing sketch Ultrasonic Theremin (saved by Fritzing 0.9.1b)
breadboards: 1

parts:
  Part1 = hc-sr04
  R1 = Resistor [tolerance=±5% resistance=1k package=THT]
  Raspberry_Pi1 = Raspberry Pi B+

nets:
  VCC: Part1.VCC, Raspberry_Pi1.5V
  N1: Part1.Trig, Raspberry_Pi1.GPIO17
  N2: Part1.Echo, R1.Pin_1
  GND: Part1.GND, Raspberry_Pi1.GND
  N3: R1.Pin_0, Raspberry_Pi1.GPIO18
