# Fritzing sketch Sample Box (saved by Fritzing 0.9.1b)
breadboards: 1

parts:
  S1 = Pushbutton [package="[THT]"]
  S2 = Pushbutton [package="[THT]"]
  S3 = Pushbutton [package="[THT]"]
  Raspberry_Pi1 = Raspberry Pi B+

nets:
  N1: S1.Pin_1, S1.Pin_2, Raspberry_Pi1.GPIO4
  N2: S1.Pin_3, S1.Pin_4, S2.Pin_3, S2.Pin_4, S3.Pin_3, S3.Pin_4, Raspberry_Pi1.GND
  N3: S2.Pin_1, S2.Pin_2, Raspberry_Pi1.GPIO3
  N4: S3.Pin_1, S3.Pin_2, Raspberry_Pi1.GPIO2
